# Fritzing sketch Joystick (saved by Fritzing 0.9.3b)
breadboards: 2

parts:
  Часть1 = Arduino Motor Shield (Rev3)  # not connected
  Часть2 = Arduino Leonardo (Rev3b)
  R1 = Rotary Potentiometer (Small) [maximum_resistance=100kΩ package=THT]
  S1 = Pushbutton [package="[THT]"]
  Часть3 = NRF24L01+ Breakout Board  # not connected
  Часть4 = Thumb Joystick  # not connected
  S2 = Toggle Switch [package=THT]  # not connected
  S3 = Toggle Switch [package=THT]  # not connected
  Dot_Matrix1 = LED Dot Matrix 18mm (0.7 INCH)  # not connected
  J1 = Basic Servo  # not connected
  M1 = DC Motor  # not connected
  M2 = DC Motor  # not connected
  VCC2 = Battery block 9V  # not connected
  VCC1 = 4 x AAA Battery Mount  # not connected
  U1 = L298 [package=multiwatt15_6400bgheatsink]  # not connected
  Часть5 = Arduino Uno (Rev3) - ICSP  # not connected

nets:
  N1: Часть2.D2/SDA, Часть2.SDA, S1.Pin_3, S1.Pin_4
  N2: Часть2.5V, R1.wiper
  N3: Часть2.GND, R1.leg2, S1.Pin_1, S1.Pin_2
  N4: Часть2.A0, R1.leg1
